# Fritzing sketch EmonTX_ADS115 (saved by Fritzing 0.9.2b)
stripboards: 1

parts:
  R109 = Resistor [tolerance=±5% resistance=22 package=THT]
  R110 = Resistor [tolerance=±5% resistance=22 package=THT]
  R111 = Resistor [tolerance=±5% resistance=22 package=THT]
  R112 = Resistor [tolerance=±5% resistance=22 package=THT]
  R113 = Resistor [tolerance=±5% resistance=22 package=THT]
  J28 = screw terminal, 2 pins
  J29 = screw terminal, 2 pins
  J30 = screw terminal, 2 pins
  J31 = screw terminal, 2 pins
  J32 = screw terminal, 2 pins
  C34 = Electrolytic Capacitor [capacitance=10µF package="100 mil [THT, electrolytic]"]
  C35 = Electrolytic Capacitor [capacitance=10µF package="100 mil [THT, electrolytic]"]
  C36 = Electrolytic Capacitor [capacitance=10µF package="100 mil [THT, electrolytic]"]
  C37 = Electrolytic Capacitor [capacitance=10µF package="100 mil [THT, electrolytic]"]
  C38 = Electrolytic Capacitor [capacitance=10µF package="100 mil [THT, electrolytic]"]
  R138 = Resistor [tolerance=±5% resistance=22 package=THT]
  R139 = Resistor [tolerance=±5% resistance=22 package=THT]
  R140 = Resistor [tolerance=±5% resistance=22 package=THT]
  R141 = Resistor [tolerance=±5% resistance=22 package=THT]
  J40 = screw terminal, 2 pins
  J41 = screw terminal, 2 pins
  J42 = screw terminal, 2 pins
  J43 = screw terminal, 2 pins
  C44 = Electrolytic Capacitor [capacitance=10µF package="100 mil [THT, electrolytic]"]
  C45 = Electrolytic Capacitor [capacitance=10µF package="100 mil [THT, electrolytic]"]
  C46 = Electrolytic Capacitor [capacitance=10µF package="100 mil [THT, electrolytic]"]
  C47 = Electrolytic Capacitor [capacitance=10µF package="100 mil [THT, electrolytic]"]
  R105 = Resistor [tolerance=±5% resistance=100k package=THT]
  R102 = Resistor [tolerance=±5% resistance=100k package=THT]
  R104 = Resistor [tolerance=±5% resistance=100k package=THT]
  R108 = Resistor [tolerance=±5% resistance=100k package=THT]
  R107 = Resistor [tolerance=±5% resistance=100k package=THT]
  R103 = Resistor [tolerance=±5% resistance=100k package=THT]
  R114 = Resistor [tolerance=±5% resistance=100k package=THT]
  R101 = Resistor [tolerance=±5% resistance=100k package=THT]
  R135 = Resistor [tolerance=±5% resistance=100k package=THT]
  R133 = Resistor [tolerance=±5% resistance=100k package=THT]
  R100 = Resistor [tolerance=±5% resistance=100k package=THT]
  R106 = Resistor [tolerance=±5% resistance=100k package=THT]
  R137 = Resistor [tolerance=±5% resistance=100k package=THT]
  R134 = Resistor [tolerance=±5% resistance=100k package=THT]
  R142 = Resistor [tolerance=±5% resistance=100k package=THT]
  R136 = Resistor [tolerance=±5% resistance=100k package=THT]
  R131 = Resistor [tolerance=±5% resistance=100k package=THT]
  R132 = Resistor [tolerance=±5% resistance=100k package=THT]
  Composant1 = ADS1115
  Raspberry_Pi1 = Raspberry Pi 2  # not connected
  Composant2 = Adafruit T-Cobbler Plus [part_number="Adafruit #1989 and #2028"]  # not connected
  Composant3 = ADS1115
  Rpullup_1wire = Resistor [tolerance=±5% resistance=4.7k package=THT]
  DS1 = DS18B20 1-Wire Temperature Sensor Probe Cable
  J44 = female pin header, 3 pins [form="♀ (female)"]

nets:
  N1: R109.Pin_0, J28.pin2, Composant3.A0
  N2: R109.Pin_1, J28.pin1, C38.+, R105.Pin_0, R102.Pin_1
  N3: R110.Pin_0, J30.pin2, Composant3.A1
  N4: R110.Pin_1, J30.pin1, C36.+, R107.Pin_1, R103.Pin_0
  N5: R111.Pin_0, J31.pin2, Composant3.A2
  N6: R111.Pin_1, J31.pin1, C35.+, R114.Pin_1, R101.Pin_0
  N7: R112.Pin_0, J29.pin2, Composant3.A3
  N8: R112.Pin_1, J29.pin1, C34.+, R100.Pin_0, R106.Pin_1
  N9: R113.Pin_0, J32.pin2, Composant3.SDA
  N10: R113.Pin_1, J32.pin1, C37.+, R104.Pin_0, R108.Pin_1
  GND: C34.-, C35.-, C36.-, C37.-, C38.-, C44.-, C45.-, C46.-, C47.-, R105.Pin_1, R104.Pin_1, R103.Pin_1, R101.Pin_1, R135.Pin_1, R100.Pin_1, R134.Pin_1, R131.Pin_1, R132.Pin_1, Composant1.GND, Composant3.GND
  N11: R138.Pin_0, J40.pin2, Composant1.A0
  N12: R138.Pin_1, J40.pin1, C47.+, R135.Pin_0, R133.Pin_1
  N13: R139.Pin_0, J42.pin2, Composant1.A1
  N14: R139.Pin_1, J42.pin1, C46.+, R137.Pin_1, R134.Pin_0
  N15: R140.Pin_0, J43.pin2, Composant1.A2
  N16: R140.Pin_1, J43.pin1, C45.+, R142.Pin_1, R132.Pin_0
  N17: R141.Pin_0, J41.pin2, Composant1.A3
  N18: R141.Pin_1, J41.pin1, C44.+, R136.Pin_1, R131.Pin_0
  VDD: R102.Pin_0, R108.Pin_0, R107.Pin_0, R114.Pin_0, R133.Pin_0, R106.Pin_0, R137.Pin_0, R142.Pin_0, R136.Pin_0, Composant1.VDD, Composant3.VDD
  N19: Composant1.SCL, Composant3.SCL
  N20: Rpullup_1wire.Pin_0, DS1.GND, DS1.shield, J44.pin1, J44.pin2
  N21: Rpullup_1wire.Pin_1, DS1.VDD, J44.pin3

notes:
  A9 (Volt)
  A1 A8
  1 WIRE
  I2C

custom parts:
  ADS1115: ADC ADS1115
  Adafruit T-Cobbler Plus: The Raspberry Pi has landed on the Maker World like a 40-GPIO pinned, quad-USB ported, credit card sized bomb of DIY joy. And while you can use most of our great Model B accessories by hooking up our downgrade cable, its probably a good time to upgrade your set up and accessorize using all of the 40 pins. That's why we now carry the Assembled Adafruit Pi T-Cobbler Plus - Breakout + Cable for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
